# Fritzing sketch ±9V_PSU (saved by Fritzing 0.9.3b)
breadboards: 3

parts:
  U1 = Voltage Regulator - 5V [package="TO220 [THT]"]
  D1 = Rectifier Diode [part_number=1N4001 package="300 mil [THT]"]
  C1 = Ceramic Capacitor [capacitance=100nF package="100 mil [THT, multilayer]"]
  C2 = Ceramic Capacitor [capacitance=100nF package="100 mil [THT, multilayer]"]
  C3 = Electrolytic Capacitor [capacitance=1µF package="100 mil [THT, electrolytic]"]
  D3 = Rectifier Diode [part_number=1N4001 package="300 mil [THT]"]
  R1 = Resistor [tolerance=±5% resistance=4.7k package=THT]
  LED1 = LED - 3mm [color="Blue (525nm)" package="3 mm [THT]"]
  U3 = Voltage Regulator - 5V [package="TO220 [THT]"]
  C4 = Electrolytic Capacitor [capacitance=1µF package="100 mil [THT, electrolytic]"]
  D5 = Rectifier Diode [part_number=1N4001 package="300 mil [THT]"]
  C5 = Ceramic Capacitor [capacitance=100nF package="100 mil [THT, multilayer]"]
  C6 = Ceramic Capacitor [capacitance=100nF package="100 mil [THT, multilayer]"]
  C7 = Electrolytic Capacitor [capacitance=1µF package="100 mil [THT, electrolytic]"]
  R2 = Resistor [tolerance=±5% resistance=4.7k package=THT]
  LED2 = LED - 3mm [color="Blue (525nm)" package="3 mm [THT]"]
  D6 = Rectifier Diode [part_number=1N4001 package="300 mil [THT]"]
  C10 = Electrolytic Capacitor [capacitance=1µF package="100 mil [THT, electrolytic]"]
  U5 = mystery part, 6 pins [chip_label="Bridge D"]
  U6 = mystery part, 4 pins [chip_label=Trans]
  R3 = Resistor [tolerance=±5% resistance=100 package=THT]
  R4 = Resistor [tolerance=±5% resistance=100 package=THT]
  R5 = Resistor [tolerance=±5% resistance=220 package=THT]
  R6 = Resistor [tolerance=±5% resistance=220 package=THT]

nets:
  N1: U1.input_voltage, D1.cathode, C1.1, C3.+, U5.pin4, R5.Pin_1
  N2: U1.GND, C1.0, C2.1, C3.-, D3.anode, R1.Pin_1, U3.input_voltage, C4.+, C5.0, C6.1, C7.+, R2.Pin_1, D6.cathode, C10.-, U6.pin2, U6.pin3, R3.Pin_0, R4.Pin_1, R5.Pin_0, R6.Pin_1
  N3: U1.output_voltage, D1.anode, C2.0, D3.cathode, LED1.anode, C10.+, R3.Pin_1
  N4: R1.Pin_0, LED1.cathode
  N5: U3.GND, C4.-, D5.anode, C5.1, U5.pin6, R6.Pin_0
  N6: U3.output_voltage, D5.cathode, C6.0, C7.-, LED2.cathode, D6.anode, R4.Pin_0
  N7: R2.Pin_0, LED2.anode
  N8: U5.pin1, U6.pin4
  N9: U5.pin3, U6.pin1

notes:
  GND
  +12V
  GND
  +9V
  -12V
  GND
  -9V
  GND
  Load:
  100ohm
  ->90mA
  Load:
  100ohm
  ->-90mA
  Load:
  220ohm
  ->54mA
  Load:
  220ohm
  ->-54mA
