# Fritzing sketch LME49600 HPA Test (saved by Fritzing 0.9.2b)
breadboards: 1

parts:
  IC1 = Dual Op-Amp [package=dip08]
  R1 = Resistor [tolerance=±5% resistance=1k package=THT]
  R2 = Resistor [tolerance=±5% resistance=1k package=THT]
  R3 = Resistor [tolerance=±5% resistance=1k package=THT]
  C1 = Ceramic Capacitor [capacitance=100nF package="100 mil [THT, multilayer]"]
  R4 = Resistor [tolerance=±5% resistance=1M package=THT]
  C2 = Ceramic Capacitor [capacitance=100nF package="100 mil [THT, multilayer]"]
  R5 = Resistor [tolerance=±5% resistance=1M package=THT]
  U1 = mystery part, 5 pins [chip_label=LME49600]
  C3 = Ceramic Capacitor [capacitance=100nF package="100 mil [THT, multilayer]"]
  C5 = Electrolytic Capacitor [capacitance=1µF package="100 mil [THT, electrolytic]"]
  C6 = Ceramic Capacitor [capacitance=100nF package="100 mil [THT, multilayer]"]
  C7 = Electrolytic Capacitor [capacitance=1µF package="100 mil [THT, electrolytic]"]
  C8 = Ceramic Capacitor [capacitance=100nF package="100 mil [THT, multilayer]"]
  C9 = Ceramic Capacitor [capacitance=100nF package="100 mil [THT, multilayer]"]
  C10 = Electrolytic Capacitor [capacitance=1µF package="100 mil [THT, electrolytic]"]
  C11 = Electrolytic Capacitor [capacitance=1µF package="100 mil [THT, electrolytic]"]
  R6 = Resistor [tolerance=±5% resistance=0 package=THT]

nets:
  N1: IC1.A_OUT, U1.pin2
  N2: IC1.A_-IN, R1.Pin_0, R2.Pin_1, R3.Pin_1
  N3: IC1.A_V-, U1.pin1, U1.pin3, C6.1, C7.-, C8.0, C11.-
  N4: IC1.B_+IN, C2.0, R5.Pin_1
  N5: IC1.B_-IN, C1.1, R4.Pin_1
  N6: IC1.B_OUT, R3.Pin_0, C1.0, R6.Pin_1
  N7: IC1.A_V+, C9.1, C10.+
  N8: R1.Pin_1, R4.Pin_0, C2.1, C3.1, C5.-, C6.0, C7.+, C8.1, C9.0, C10.-, C11.+, R6.Pin_0
  N9: R2.Pin_0, R5.Pin_0, U1.pin4
  N10: U1.pin5, C3.0, C5.+

notes:
  LME49600
  1 BW
  2 VIN
  3 VEE
  4 VOUT
  5 VCC
  V-
  GND
  GND
  V+
  IN
  OUT
