# Fritzing sketch LME49600 buffer test (saved by Fritzing 0.9.2b)
breadboards: 1

parts:
  U1 = mystery part, 5 pins [chip_label=LME49600]
  C3 = Ceramic Capacitor [capacitance=100nF package="100 mil [THT, multilayer]"]
  C5 = Electrolytic Capacitor [capacitance=1µF package="100 mil [THT, electrolytic]"]
  C6 = Ceramic Capacitor [capacitance=100nF package="100 mil [THT, multilayer]"]
  C7 = Electrolytic Capacitor [capacitance=1µF package="100 mil [THT, electrolytic]"]
  C10 = Electrolytic Capacitor [capacitance=1µF package="100 mil [THT, electrolytic]"]
  C11 = Electrolytic Capacitor [capacitance=1µF package="100 mil [THT, electrolytic]"]
  R1 = Resistor [tolerance=±5% resistance=100 package=THT]
  C12 = Ceramic Capacitor [capacitance=100nF package="100 mil [THT, multilayer]"]

nets:
  N1: U1.pin1, U1.pin3, C6.1, C7.-, C11.-, C12.1
  N2: U1.pin4, R1.Pin_0, C12.0
  N3: U1.pin5, C3.0, C5.+
  N4: C3.1, C5.-, C6.0, C7.+, C10.-, C11.+, R1.Pin_1

notes:
  LME49600
  1 BW
  2 VIN
  3 VEE
  4 VOUT
  5 VCC
  V-
  GND
  GND
  V+
  IN
  OUT
